# Fritzing sketch FaceBot (saved by Fritzing 0.9.3b)

parts:
  M1 = DC Motor
  M2 = DC Motor
  Part2 = Adafruit Circuit Playground Express [part_number="Adafruit #3333"]
  MCU1 = Raspberry Pi Zero
  Part3 = Adafruit Crickit for Circuit Playground Express [part_number="Adafruit #3093"]

nets:
  N1: M1.pin_1, Part3.MOTOR_1A_OUT
  N2: M1.pin_2, Part3.MOTOR_1B_OUT
  N3: M2.pin_1, Part3.MOTOR_2A_OUT
  N4: M2.pin_2, Part3.MOTOR_2B_OUT
  N5: Part2.D6_A1, Part3.CPX_A1
  GND: Part2.GND, MCU1.pin_6, MCU1.pin_25, Part3.GND
  N6: Part2.D12_A0_SPEAKER, Part3.CPX_A0
  N7: Part2.D0_A6_RX, MCU1.pin_8
  N8: Part2.D3_A4_SCL, Part3.CPX_SCL
  N9: Part2.D2_A5_SDA, Part3.CPX_SDA
  N10: Part2.D1_A7_TX, MCU1.pin_10
  N11: Part2.VOUT, Part3.CPX_VOUT

custom parts:
  Adafruit Circuit Playground Express: Circuit Playground Express is the next step towards a perfect introduction to electronics and programming. We've taken the original Circuit Playground Classic and made it even better! Not only did we pack even more sensors in, we also made it even easier to program. You can now start your journey with Microsoft MakeCode block-based or Javascript programming. Then, you can use the same board to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
  Adafruit Crickit for Circuit Playground Express: Sometimes we wonder if robotics engineers ever watch movies. If they did, they'd know that making robots into slaves always ends up in a robot rebellion. Why even go down that path? Here at Adafruit, we believe in making robots our friends! So if you find yourself wanting a companion, consider the robot. They're fun to program, and you can get creative with decorations. With that in mind, we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
